# Fritzing sketch ConectorWifiX10 (saved by Fritzing 0.9.2b)
circuit board: 8.46667cm x 5.64444cm
breadboards: 1

parts:
  R1 = Resistor [tolerance=±5% resistance=10k package=THT]
  J1 = screw terminal, 8 pins
  Parte1 = Arduino Uno (Rev3) - ICSP

nets:
  N1: R1.Pin_0, J1.pin2, Parte1.5V
  N2: R1.Pin_1, J1.pin5, Parte1.D3_PWM
  N3: J1.pin1, J1.pin4, Parte1.GND
  N4: J1.pin3, Parte1.D2
