# Fritzing sketch ConectorWifiX10Sencillo (saved by Fritzing 0.9.2b)
circuit board: 6.95275cm x 5.3852cm
breadboards: 1

parts:
  R1 = Resistor [tolerance=±5% resistance=10k package=THT]
  Parte1 = Arduino Uno (Rev3) - ICSP
  J1 = screw terminal, 4 pins

nets:
  N1: R1.Pin_0, Parte1.5V
  N2: R1.Pin_1, Parte1.D3_PWM, J1.pin1
  N3: Parte1.GND, J1.pin3
  N4: Parte1.D2, J1.pin2
